# Fritzing sketch development-layout1 (saved by Fritzing 0.9.3b)
breadboards: 2

parts:
  Mod1 = Raspberry Pi Pico W
  U1 = MT3608 DC-DC Buck converter [package=THT]
  JP1 = Header 2 [package=screwterminal-3.5mm-2_lock]
  U2 = Mini-360 DC-DC Buck converter [package=THT]
  VCC1 = Lead Acid Battery 4V
  IC1 = ULN2003A [package="DIP16 [THT]"]
  U3 = SN-GCJA5 Laser Type PM Sensor [package=THT]
  R1 = Resistor [tolerance=±2% resistance=30k package=THT]
  R2 = Resistor [tolerance=±2% resistance=20k package=THT]
  SPS1 = SPS30 Particulate Matter Sensor for Air Quality Monitoring and Control [package=THT]
  Часть2 = BMP180 Breakout (GY-68)
  Componente1 = Adafruit SHT31-D [part_number="Adafruit #2857"]

nets:
  N1: Mod1.pin_1, U3.SDA_I2C, SPS1.SDA_I2C_/UART_RX, Часть2.SDA, Componente1.SDA
  N2: Mod1.pin_2, U3.SCL_I2C, SPS1.SCL_I2C_/_UART_TX, Часть2.SCL, Componente1.SCL
  GND: Mod1.pin_3, Mod1.pin_33, Mod1.pin_38, Mod1.pin_42, U1.IN-, U1.OUT-, U2.OUT-, VCC1.-, IC1.0V, R1.Pin_0, Часть2.GND, Componente1.GND
  N3: Mod1.pin_4, IC1.In_7
  N4: Mod1.pin_5, IC1.In_6
  N5: Mod1.pin_6, IC1.In_5
  N6: Mod1.pin_7, IC1.In_4
  N7: Mod1.pin_9, IC1.In_3
  N8: Mod1.pin_10, IC1.In_2
  N9: Mod1.pin_11, IC1.In_1
  N10: Mod1.pin_34, R2.Pin_0
  VCC: Mod1.pin_36, Часть2.VCC, Componente1.VCC
  N11: Mod1.pin_39, U1.IN+, U2.OUT+, VCC1.+, R2.Pin_1
  5V: U1.OUT+, IC1.COM_-_Common, U3.5V, SPS1.VDD
  N12: JP1.-, U2.IN-
  N13: JP1.+, U2.IN+
  N14: IC1.Out_7, U3.GND
  N15: IC1.Out_6, SPS1.GND, SPS1.Interface_select

notes:
  output: 4.7 V
  for 4V battery
  1.5 A max
  I2C bus
  0 3v3
  1 SDA
  2 SCL
  3 GND
  4 5V
  output: 5.9 V
  for 5V sensors
  (-0.9 voltage drop across ULN2003)

custom parts:
  Raspberry Pi Pico W: Raspberry Pi Pico W. Based around the RP2040 microcontroller the Pico W is a low cost microcontroller device bringing Raspberry Pi quality, cost, and easy of use to the microcontroller space. The areas marked KEEPOUT in pcb silkscreen should not have traces running through them to avoid shorts on a soldered in module!
  MT3608 DC-DC Buck converter: MT3608 DC-DC Boost converter. Tiny step up voltage converter, input voltage 2 to 24V output 1 to 28V adjustable. When connecting for the first time in order to set the desird voltage, use a very low voltage input eg. 4v, better if limiting the current. Available from ebay and the like.
  Header 2: Header 2 Standard 2-pin 0.1 header. Use with straight break away headers (SKU : PRT-00116), right angle break away headers (PRT-00553), swiss pins (PRT-00743), machine pins (PRT-00117), and female headers (PRT-00115). Molex polarized connector foot print use with SKU : PRT-08233 with associated crimp pins and housings.
  Mini-360 DC-DC Buck converter: Mini-360 DC-DC Buck converter. Tiny buck step down voltage converter, input voltage 4.75 to 23V output 1 to 17V adjustable. Available from ebay and the like.
  Lead Acid Battery 4V: 4 Volts battery block
  SN-GCJA5 Laser Type PM Sensor: Laser Type PM Sensor
  SPS30 Particulate Matter Sensor for Air Quality Monitoring and Control: Laser Type PM Sensor
  BMP180 Breakout (GY-68): This is a simple breakout board for the BMP180, a high-precision, low-power barometric pressure sensor made by Bosch Sensortec. The range of measurement is from 300hPa to 1100hPa. The sensor can be supplied with voltage ranging from 1.8V to 3.6V. Operating temperature range is -40 to +85 °C. This particular breakout board (or perhaps the configuration) is produced by Shenzhen Keep Power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
  Adafruit SHT31-D: Sensirion Temperature/Humidity sensors are some of the finest & highest-accuracy devices you can get. And, finally we have some that have a true I2C interface for easy reading. The SHT31-D sensor has an excellent ±2% relative humidity and ±0.3°C accuracy for most uses. We now use the version with a PTFE filter, it'll stay clean while still allowing humidity measurements to work Unlike earlier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
